# Fritzing sketch arduinoNFLFritzing (saved by Fritzing 0.9.2b)
breadboards: 1

parts:
  Part1 = Arduino Uno (Rev3)
  LCD1 = LCD screen
  R2 = Trimmer Potentiometer [maximum_resistance=10kΩ package=THT]
  R3 = Resistor [tolerance=±5% resistance=220 power=220 package=THT]
  S1 = Pushbutton [package="[THT]"]
  S2 = Pushbutton [package="[THT]"]
  R4 = Resistor [tolerance=±5% resistance=220 package=THT]
  R5 = Resistor [tolerance=±5% resistance=220 package=THT]

nets:
  N1: Part1.D8, LCD1.E
  N2: Part1.D9_PWM, LCD1.DB4
  N3: Part1.D10_PWM/SS, LCD1.DB5
  N4: Part1.D11_PWM/MOSI, LCD1.DB6
  N5: Part1.D12/MISO, LCD1.DB7
  5V: Part1.D5_PWM, Part1.D6_PWM, Part1.5V, LCD1.VDD, R2.leg2, R3.Pin_0, S1.Pin_1, S1.Pin_2, S2.Pin_1, S2.Pin_2, R4.Pin_0, R5.Pin_0
  N6: Part1.D7, LCD1.RS
  GND: Part1.GND, LCD1.VSS, LCD1.R/W, LCD1.LED-, R2.leg1
  N7: LCD1.V0, R2.wiper
  N8: LCD1.LED+, R3.Pin_1
  N9: S1.Pin_3, S1.Pin_4, R4.Pin_1
  N10: S2.Pin_3, S2.Pin_4, R5.Pin_1
